# Fritzing sketch SchemaLedStrip (saved by Fritzing 0.9.10b)
perfboards: 1

parts:
  Q1_(IRLZ34N) = Basic FET N-Channel [package="D2Pak [SMD]"]
  Componente1 = Arduino Mega 2560 (Rev3)
  Q1 = Basic FET N-Channel [package="D2Pak [SMD]"]
  Q2 = Basic FET N-Channel [package="D2Pak [SMD]"]
  Q3 = Basic FET N-Channel [package="D2Pak [SMD]"]
  J2 = Camdenboss CTB0158-2 [part_number=CTB0158-2 package=THT]
  J1 = Camdenboss CTB0158-5 [part_number=CTB0158-5 package=THT]
  F1 = Fan - Ventilador [package=THT]  # not connected
  Raspberry_Pi1 = Raspberry Pi 2  # not connected

nets:
  N1: Q1_(IRLZ34N).Gate, Componente1.D6_PWM
  N2: Q1_(IRLZ34N).drain, J1.pin2
  N3: Q1_(IRLZ34N).source, J2.pin1
  N4: Componente1.D3_PWM, Q3.Gate
  N5: Componente1.D4_PWM, Q2.Gate
  N6: Componente1.D5_PWM, Q1.Gate
  N7: Q1.drain, J1.pin3
  N8: Q2.drain, J1.pin4
  N9: Q3.drain, J1.pin5
  N10: J2.pin2, J1.pin1

notes:
  Alimentatore -
  12v +
  Case Fan

custom parts:
  Fan - Ventilador: Ventilador de 2 pines, se encuentra comunmente en computadoras de escritorio
